# Fritzing sketch MqttPir (saved by Fritzing 0.9.3b)
breadboards: 1

parts:
  U1 = ESP8266 NodeMCU LoLin module
  R1 = Resistor [tolerance=±5% resistance=330k package=THT]
  S1 = SWITCH-MOMENTARY-2 [package=tactile-switch-1101ne]

nets:
  N1: U1.D5, S1.1
  N2: U1.GND, R1.Pin_1, S1.2
  N3: U1.3V3, R1.Pin_0

custom parts:
  ESP8266 NodeMCU LoLin module: ESP8266 based NodeMCU
